// Logisim project Sub_4.circ as structural Verilog: 5 circuits, main circuit main
module main (
  input  [3:0] A,
  input  [3:0] B,
  input  A_2,
  input  B_2,
  input  C,
  output out_6,
  output VAI_1,
  output [3:0] out_8,
  output S
);

  ADD_1 add_1_1 (.S(S), .Vai_1(VAI_1), .A(A_2), .B(B_2), .C(C));
  // Add_4 add_4_1: pin names not known; wires that end beside it: out_6, A, out_8, B
endmodule

module ADD_1 (
  input  A,
  input  B,
  input  C,
  output S,
  output Vai_1
);

  wire and_1_out, and_2_out, or_1_out, xor_1_out;

  or or_1 (or_1_out, C, B);
  xor xor_1 (xor_1_out, C, B);
  and and_1 (and_1_out, or_1_out, A);
  and and_2 (and_2_out, C, B);
  xor xor_2 (S, xor_1_out, A);
  or or_2 (Vai_1, and_1_out, and_2_out);
endmodule

module Add_4 (
  input  [3:0] B,
  input  [3:0] A,
  output Overflow,
  output [3:0] S
);

  wire add_1_2_vai_1, add_1_3_vai_1, add_1_4_vai_1;

  ADD_1 add_1_1 (.S(S[3]), .Vai_1(Overflow), .A(A[3]), .B(B[3]), .C(add_1_2_vai_1));
  ADD_1 add_1_2 (.S(S[2]), .Vai_1(add_1_2_vai_1), .A(A[2]), .B(B[2]), .C(add_1_3_vai_1));
  ADD_1 add_1_3 (.S(S[1]), .Vai_1(add_1_3_vai_1), .A(A[1]), .B(B[1]), .C(add_1_4_vai_1));
  ADD_1 add_1_4 (.S(S[0]), .Vai_1(add_1_4_vai_1), .A(A[0]), .B(B[0]), .C(1'b0));
endmodule

module Sub_1 (
  input  A,
  input  B,
  input  VEM_1,
  output S,
  output Vai_1
);

  wire and_1_out, and_2_out, or_1_out, xor_1_out;

  or or_1 (or_1_out, B, VEM_1);
  xor xor_1 (xor_1_out, A, B);
  and and_1 (and_1_out, or_1_out, ~A);  // AND_Gate
  and and_2 (and_2_out, VEM_1, B);
  xor xor_2 (S, xor_1_out, VEM_1);
  or or_2 (Vai_1, and_1_out, and_2_out);
endmodule

module Sub_4 (
  input  [3:0] B,
  input  [3:0] A,
  output Overflow,
  output [3:0] S
);

  wire sub_1_2_vai_1, sub_1_3_vai_1, sub_1_4_vai_1;

  // Probe on A
  Sub_1 sub_1_1 (.S(S[3]), .Vai_1(Overflow), .A(A[3]), .B(B[3]), .VEM_1(sub_1_2_vai_1));
  Sub_1 sub_1_2 (.S(S[2]), .Vai_1(sub_1_2_vai_1), .A(A[2]), .B(B[2]), .VEM_1(sub_1_3_vai_1));
  Sub_1 sub_1_3 (.S(S[1]), .Vai_1(sub_1_3_vai_1), .A(A[1]), .B(B[1]), .VEM_1(sub_1_4_vai_1));
  // Probe on S
  Sub_1 sub_1_4 (.S(S[0]), .Vai_1(sub_1_4_vai_1), .A(A[0]), .B(B[0]), .VEM_1(1'b0));
  // Probe on B
endmodule
